# Fritzing sketch Button Sketch2 (saved by Fritzing 0.9.1b)
breadboards: 1

parts:
  U1 = XBee
  Parte1 = Arduino Uno (Rev3)
  R1 = Resistor [tolerance=±5% resistance=10k package="0603 [SMD]"]
  S1 = Pushbutton [package="[THT]"]

nets:
  VCC: U1.VCC, Parte1.3V3
  N1: U1.pin2, Parte1.D0/RX
  N2: U1.pin3, Parte1.D1/TX
  GND: U1.GND, Parte1.GND
  N3: Parte1.D2, R1.Pin_0, S1.Pin_1, S1.Pin_2
  N4: S1.Pin_3, S1.Pin_4
