# Fritzing sketch Buzzer Sketch (saved by Fritzing 0.9.1b)
breadboards: 1

parts:
  U1 = XBee
  Parte1 = Arduino Uno (Rev3)
  J1 = Piezo Speaker

nets:
  VCC: U1.VCC, Parte1.3V3
  N1: U1.pin2, Parte1.D0/RX
  N2: U1.pin3, Parte1.D1/TX
  GND: U1.GND, Parte1.GND
  N3: Parte1.D5_PWM, J1.pin2
